# Fritzing sketch Arduino Smart Control (saved by Fritzing 0.9.3b)
breadboards: 1

parts:
  Componente1 = Arduino Nano (Rev3.0)
  LED1 = LED - 5mm [color="Red (633nm)" package="5 mm [THT]"]
  LED2 = LED - 5mm [color="Orange (612nm)" package="5 mm [THT]"]
  LED3 = LED - 5mm [color="Yellow (585nm)" package="5 mm [THT]"]
  LED4 = LED - 5mm [color="Green (565nm)" package="5 mm [THT]"]
  R1 = Resistor [tolerance=±5% resistance=220 package=THT]
  R2 = Resistor [tolerance=±5% resistance=220 package=THT]
  R3 = Resistor [tolerance=±5% resistance=220 package=THT]
  R4 = Resistor [tolerance=±5% resistance=220 package=THT]
  RHT1 = Humidity and Temperature Sensor RHT03
  R5 = Photocell (LDR) [package=THT]
  R6 = Resistor [tolerance=±5% resistance=100k package=THT]

nets:
  N1: Componente1.D4, RHT1.Data-signal
  N2: Componente1.D5, R4.Pin_0
  N3: Componente1.D6, R3.Pin_0
  N4: Componente1.D7, R2.Pin_0
  N5: Componente1.D8, R1.Pin_0
  N6: Componente1.5V, R5.pin_0
  N7: Componente1.A0, R5.pin_1, R6.Pin_1
  N8: Componente1.3V3, RHT1.GND_2
  N9: LED1.cathode, LED2.cathode, LED3.cathode, LED4.cathode, RHT1.Vcc, R6.Pin_0
  N10: LED1.anode, R1.Pin_1
  N11: LED2.anode, R2.Pin_1
  N12: LED3.anode, R3.Pin_1
  N13: LED4.anode, R4.Pin_1
